# Fritzing sketch Signal_Circuit (saved by Fritzing 0.9.3b)
circuit board: 10cm x 6cm
breadboards: 1

parts:
  U1 = RELAY [package=relay-jzc]
  U2 = RELAY [package=relay-jzc]
  U3 = RELAY [package=relay-jzc]
  U4 = RELAY [package=relay-jzc]
  D1 = Rectifier Diode [part_number=1N4001 package="Melf DO-213 AB [SMD]"]
  Q1 = NPN-Transistor [package="SOT-23 [SMD]"]
  D2 = Rectifier Diode [part_number=1N4001 package="Melf DO-213 AB [SMD]"]
  D3 = Rectifier Diode [part_number=1N4001 package="Melf DO-213 AB [SMD]"]
  D4 = Rectifier Diode [part_number=1N4001 package="Melf DO-213 AB [SMD]"]
  Q2 = NPN-Transistor [package="SOT-23 [SMD]"]
  Q3 = NPN-Transistor [package="SOT-23 [SMD]"]
  Q4 = NPN-Transistor [package="SOT-23 [SMD]"]
  R1 = Resistor [tolerance=±5% resistance=220 package=THT]
  R2 = Resistor [tolerance=±5% resistance=220 package=THT]
  R3 = Resistor [tolerance=±5% resistance=220 package=THT]
  R4 = Resistor [tolerance=±5% resistance=220 package=THT]
  D5 = Rectifier Diode [part_number=1N4001 package="Melf DO-213 AB [SMD]"]
  D6 = Rectifier Diode [part_number=1N4001 package="Melf DO-213 AB [SMD]"]
  D7 = Rectifier Diode [part_number=1N4001 package="Melf DO-213 AB [SMD]"]
  D8 = Rectifier Diode [part_number=1N4001 package="Melf DO-213 AB [SMD]"]

nets:
  GND: U1.COIL2, U2.COIL2, U3.COIL2, U4.COIL2
  Output: U1.NO, U2.NO, U3.NO, U4.NO
  N1: U1.MAIN, D5.cathode
  N2: U1.COIL1, D1.cathode
  N3: U2.MAIN, D6.cathode
  N4: U2.COIL1, D2.cathode
  N5: U3.MAIN, D7.cathode
  N6: U3.COIL1, D3.cathode
  N7: U4.MAIN, D8.cathode
  N8: U4.COIL1, D4.cathode
  N9: D1.anode, Q1.2
  N10: Q1.0, R1.Pin_1
  5V: Q1.1, Q2.1, Q3.1, Q4.1
  N11: D2.anode, Q2.2
  N12: D3.anode, Q3.2
  N13: D4.anode, Q4.2
  N14: Q2.0, R2.Pin_1
  N15: Q3.0, R3.Pin_1
  N16: Q4.0, R4.Pin_1
  cSignalOne: R1.Pin_0
  cSignalTwo: R2.Pin_0
  cSignalThree: R3.Pin_0
  cSignalFor: R4.Pin_0
  Signal 1: D5.anode
  Signal 2: D6.anode
  Signal 3: D7.anode
  Signal 4: D8.anode
