# Fritzing sketch Signal_Circuit (saved by Fritzing 0.9.3b)
circuit board: 13.5063cm x 10.4649cm
circuit board: 13.5063cm x 10.4649cm
breadboards: 1

parts:
  U2 = RELAY [package=relay-jzc]
  U3 = RELAY [package=relay-jzc]
  U4 = RELAY [package=relay-jzc]
  R1 = Resistor [tolerance=±5% resistance=220 package=THT]
  R2 = Resistor [tolerance=±5% resistance=220 package=THT]
  R3 = Resistor [tolerance=±5% resistance=220 package=THT]
  R4 = Resistor [tolerance=±5% resistance=220 package=THT]
  U5 = RELAY [package=relay-jzc]
  U6 = RELAY [package=relay-jzc]
  U7 = RELAY [package=relay-jzc]
  U8 = RELAY [package=relay-jzc]
  R5 = Resistor [tolerance=±5% resistance=220 package=THT]
  R6 = Resistor [tolerance=±5% resistance=220 package=THT]
  R7 = Resistor [tolerance=±5% resistance=220 package=THT]
  R8 = Resistor [tolerance=±5% resistance=220 package=THT]
  J1 = Screw terminal - 2 pins [package=THT]
  U1 = RELAY [package=relay-jzc]
  Input_4 = Audio Jack (TRRS) 3.5mm [part_number=Jack package="RC-5325A [SMD]"]
  Input_3 = Audio Jack (TRRS) 3.5mm [part_number=Jack package="RC-5325A [SMD]"]
  Input_2 = Audio Jack (TRRS) 3.5mm [part_number=Jack package="RC-5325A [SMD]"]
  OUTPUT = Audio Jack (TRRS) 3.5mm [part_number=Jack package="RC-5325A [SMD]"]
  Input_1 = Audio Jack (TRRS) 3.5mm [part_number=Jack package="RC-5325A [SMD]"]
  D8 = Rectifier Diode [part_number=1N4001 package="Melf DO-213 AB [SMD]"]
  D7 = Rectifier Diode [part_number=1N4001 package="Melf DO-213 AB [SMD]"]
  D6 = Rectifier Diode [part_number=1N4001 package="Melf DO-213 AB [SMD]"]
  D5 = Rectifier Diode [part_number=1N4001 package="Melf DO-213 AB [SMD]"]
  Q4 = NPN-Transistor [package="SOT-23 [SMD]"]
  Q3 = NPN-Transistor [package="SOT-23 [SMD]"]
  D9 = Rectifier Diode [part_number=1N4001 package="Melf DO-213 AB [SMD]"]
  D10 = Rectifier Diode [part_number=1N4001 package="Melf DO-213 AB [SMD]"]
  D11 = Rectifier Diode [part_number=1N4001 package="Melf DO-213 AB [SMD]"]
  D12 = Rectifier Diode [part_number=1N4001 package="Melf DO-213 AB [SMD]"]
  Q5 = NPN-Transistor [package="SOT-23 [SMD]"]
  Q6 = NPN-Transistor [package="SOT-23 [SMD]"]
  Q7 = NPN-Transistor [package="SOT-23 [SMD]"]
  Q8 = NPN-Transistor [package="SOT-23 [SMD]"]
  Q2 = NPN-Transistor [package="SOT-23 [SMD]"]
  Q1 = NPN-Transistor [package="SOT-23 [SMD]"]

nets:
  GND: U2.COIL2, U3.COIL2, U4.COIL2, U5.COIL2, U6.COIL2, U7.COIL2, U8.COIL2, J1.pin2, U1.COIL2
  Ring 1.2: U2.NC, Input_2.RING1
  Left: U2.NO, U3.NO, U4.NO, U1.NO, OUTPUT.RING1
  N1: U2.MAIN, D6.cathode
  N2: U2.COIL1, Q2.2
  Ring 1.3: U3.NC, Input_3.RING1
  N3: U3.MAIN, D7.cathode
  N4: U3.COIL1, Q3.2
  Ring 1.4: U4.NC, Input_4.RING1
  N5: U4.MAIN, D8.cathode
  N6: U4.COIL1, Q4.2
  cSignalOneL: R1.Pin_0
  N7: R1.Pin_1, Q1.0
  cSignalTwoL: R2.Pin_0
  N8: R2.Pin_1, Q2.0
  cSignalThreeL: R3.Pin_0
  N9: R3.Pin_1, Q3.0
  cSignalForL: R4.Pin_0
  N10: R4.Pin_1, Q4.0
  Ring 2.4: U5.NC, Input_4.RING2
  Right: U5.NO, U6.NO, U7.NO, U8.NO, OUTPUT.RING2
  N11: U5.MAIN, D9.cathode
  N12: U5.COIL1, Q5.2
  Ring 2.3: U6.NC, Input_3.RING2
  N13: U6.MAIN, D10.cathode
  N14: U6.COIL1, Q6.2
  Ring 2.2: U7.NC, Input_2.RING2
  N15: U7.MAIN, D11.cathode
  N16: U7.COIL1, Q7.2
  Ring 2.1: U8.NC, Input_1.RING2
  N17: U8.MAIN, D12.cathode
  N18: U8.COIL1, Q8.2
  cSignalForR: R5.Pin_0
  N19: R5.Pin_1, Q5.0
  cSignalThreeR: R6.Pin_0
  N20: R6.Pin_1, Q6.0
  cSignalTwoR: R7.Pin_0
  N21: R7.Pin_1, Q7.0
  cSignalOneR: R8.Pin_0
  N22: R8.Pin_1, Q8.0
  5V: J1.pin1, Q4.1, Q3.1, Q5.1, Q6.1, Q7.1, Q8.1, Q2.1, Q1.1
  Ring 1.1: U1.NC, Input_1.RING1
  N23: U1.MAIN, D5.cathode
  N24: U1.COIL1, Q1.2
  Tip 4: Input_4.TIP
  Sleeve: Input_4.SLEEVE, Input_3.SLEEVE, Input_2.SLEEVE, OUTPUT.SLEEVE, Input_1.SLEEVE
  Tip 3: Input_3.TIP
  Tip 2: Input_2.TIP
  Tip 1: Input_1.TIP
  Signal 4: D8.anode
  Signal 3: D7.anode
  Signal 2: D6.anode
  Signal 1: D5.anode
  Signal 8: D9.anode
  Signal 7: D10.anode
  Signal 6: D11.anode
  Signal 5: D12.anode
