# Fritzing sketch mainArduino (saved by Fritzing 0.9.3b)
breadboards: 1

parts:
  Composant1 = Arduino Mega 2560 (Rev3)
  D3 = Rectifier Diode [part_number=1N4001 package="Melf DO-213 AB [SMD]"]

nets:
  N1: Composant1.GND, D3.anode
  12V: Composant1.VIN
  eGLRB: Composant1.D22
  eDLRB: Composant1.D23
  eGSM: Composant1.D24
  eDSM: Composant1.D25
  eGLREa: Composant1.D26
  eDLREa: Composant1.D27
  eGLREb: Composant1.D28
  eDLREb: Composant1.D29
  eLRBS: Composant1.D30
  eSMS: Composant1.D31
  eLREaS: Composant1.D32
  eLREbS: Composant1.D33
  ledOne: Composant1.D34
  ledTwo: Composant1.D35
  ledThree: Composant1.D36
  ledFor: Composant1.D37
  signalOne: Composant1.D38
  signalTwo: Composant1.D39
  signalThree: Composant1.D40
  signalFor: Composant1.D41
  cSignalOne: Composant1.D42
  cSignalTwo: Composant1.D43
  cSignalThree: Composant1.D44
  cSignalFor: Composant1.D45
  GND: D3.cathode
